// Logisim project 1-bit_Arithmetic.circ as structural Verilog: 1 circuit, main circuit 1-bit_Arithmetic
module _1_bit_Arithmetic (
  input  Cin,
  input  S0,
  input  S1,
  input  A_i,
  input  B_i,
  output D_i,
  output C_i_1
);

  wire multiplexer_1_out, not_1_out, not_2_out;

  not not_1 (not_1_out, B_i);
  not not_2 (not_2_out, 1'b0);
  Multiplexer #(.select(2)) multiplexer_1 (
    .in0(B_i), .in1(not_1_out), .in2(1'b0), .in3(not_2_out), .out(multiplexer_1_out), .sel({S1, S0}));  // open: en
  Adder #(.width(1)) adder_1 (.a(A_i), .b(multiplexer_1_out), .out(D_i), .cin(Cin), .cout(C_i_1));
endmodule
