// Logisim project 1-bit_adder.circ as structural Verilog
module _2_bitArithmetic (
  input  Cin,
  input  S0,
  input  S1,
  input  [1:0] A_i,
  input  [1:0] B_i,
  output D_i,
  output C_i_2
);

  wire n1_bit_arithmetic_1_c_i_1;

  _1_bit_Arithmetic u_1_bit_arithmetic_1 (
    .Cin(Cin), .S0(S0), .S1(S1), .A_i(A_i[0]), .B_i(B_i[0]), .D_i(D_i), .C_i_1(n1_bit_arithmetic_1_c_i_1));
  _1_bit_Arithmetic u_1_bit_arithmetic_2 (
    .Cin(n1_bit_arithmetic_1_c_i_1), .S0(S0), .S1(S1), .A_i(A_i[1]), .B_i(B_i[1]), .C_i_1(C_i_2));  // open: D_i
endmodule

module _1_bit_Logic (
  input  [1:0] S1_S0,
  input  A_i,
  input  B_i,
  output F_i
);

  wire and_1_out, not_1_out, or_1_out, xor_1_out;

  and and_1 (and_1_out, A_i, B_i);
  or or_1 (or_1_out, A_i, B_i);
  xor xor_1 (xor_1_out, A_i, B_i);
  not not_1 (not_1_out, A_i);
  Multiplexer #(.select(2)) multiplexer_1 (
    .in0(and_1_out), .in1(or_1_out), .in2(xor_1_out), .in3(not_1_out), .out(F_i), .sel(S1_S0));  // open: en
endmodule

module _2_bit_Logic (
  input  [1:0] S1_S0,
  input  [1:0] A,
  input  [1:0] B,
  output F_i,
  output F_i_1
);

  _1_bit_Logic u_1_bit_logic_1 (.S1_S0(S1_S0), .A_i(A[0]), .B_i(B[0]), .F_i(F_i));
  _1_bit_Logic u_1_bit_logic_2 (.S1_S0(S1_S0), .A_i(A[1]), .B_i(B[1]), .F_i(F_i_1));
endmodule

module ALSU (
);

  ProgramCounter programcounter_1 ();
endmodule

module _1_bit_Arithmetic (
  input  Cin,
  input  S0,
  input  S1,
  input  A_i,
  input  B_i,
  output D_i,
  output C_i_1
);

  wire multiplexer_1_out, not_1_out, not_2_out;

  not not_1 (not_1_out, B_i);
  not not_2 (not_2_out, 1'b0);
  Multiplexer #(.select(2)) multiplexer_1 (
    .in0(B_i), .in1(not_1_out), .in2(1'b0), .in3(not_2_out), .out(multiplexer_1_out), .sel({S1, S0}));  // open: en
  Adder #(.width(1)) adder_1 (.a(A_i), .b(multiplexer_1_out), .out(D_i), .cin(Cin), .cout(C_i_1));
endmodule

module ProgramCounter (
);

  wire clock_1_out, controlunit_1_pc_inc, controlunit_1_pc_out;
  wire [3:0] adder_1_out, controlled_buffer_1_out, register_1_q;

  Clock clock_1 (.out(clock_1_out));
  ControlUnit controlunit_1 (
    .PC_inc(controlunit_1_pc_inc), .PC_out(controlunit_1_pc_out));  // open: clk_in, Op2, Op1, Op0, AR_load2, AR_load, T1, IR_load, T2, T3, T4, ALU_en, LDA_active, ADD_active, OUT_active, Display_load, HLT_active, Clock_halt, RAM_out, AC_load, STA_active, STA_write, SUB_active, JMP_active, JZ_active, PC_load, SUB_en
  Register #(.width(4)) register_1 (
    .D(adder_1_out), .en(controlunit_1_pc_inc), .Q(register_1_q), .clk(clock_1_out));  // open: clr
  assign controlled_buffer_1_out = controlunit_1_pc_out ? register_1_q : 4'bz;  // Controlled_Buffer controlled_buffer_1
  Adder #(.width(4)) adder_1 (.a(register_1_q), .b(4'b0001), .out(adder_1_out));  // open: cin, cout
  Hex_Digit_Display hex_digit_display_1 (.value(register_1_q));  // open: dp
  Hex_Digit_Display hex_digit_display_2 (.value(controlled_buffer_1_out));  // open: dp
endmodule

module ControlUnit (
  input  clk_in,
  input  Op2,
  input  Op1,
  input  Op0,
  output AR_load2,
  output AR_load,
  output PC_inc,
  output T1,
  output PC_out,
  output IR_load,
  output T2,
  output T3,
  output T4,
  output ALU_en,
  output LDA_active,
  output ADD_active,
  output OUT_active,
  output Display_load,
  output HLT_active,
  output Clock_halt,
  output RAM_out,
  output AC_load,
  output STA_active,
  output STA_write,
  output SUB_active,
  output JMP_active,
  output JZ_active,
  output PC_load,
  output SUB_en
);

  wire or_1_out;
  wire [3:0] counter_1_q;

  Decoder #(.select(3)) decoder_1 (
    .out0(LDA_active), .out1(ADD_active), .out2(OUT_active), .out3(HLT_active), .out4(STA_active),
    .out5(SUB_active), .out6(JMP_active), .out7(JZ_active), .sel({Op0, Op1, Op2}));  // open: en
  Counter #(.width(4), .max('hf)) counter_1 (.Q(counter_1_q), .clk(clk_in));  // open: load, D, count, carry, clr
  Decoder #(.select(4)) decoder_2 (
    .out0(AR_load), .out1(IR_load), .out2(AR_load2), .out3(T4), .sel(counter_1_q));  // open: out4, out5, out6, out7, out8, out9, out10, out11, out12, out13, out14, out15, en
  and and_1 (ALU_en, AR_load2, ADD_active);
  or or_1 (or_1_out, ADD_active, LDA_active);
  and and_2 (Display_load, AR_load2, OUT_active);
  and and_3 (Clock_halt, AR_load2, HLT_active);
  and and_4 (AC_load, AR_load2, or_1_out);
  and and_5 (STA_write, STA_active, AR_load2);
  and and_6 (PC_load, JMP_active, AR_load2);
  and and_7 (SUB_en, SUB_active, AR_load2);

  assign PC_inc = AR_load;
  assign PC_out = AR_load;
  assign RAM_out = AC_load;
  assign T1 = AR_load;
  assign T2 = IR_load;
  assign T3 = AR_load2;
endmodule

module AR (
);

  Register #(.width(4)) AR ();  // open: D, en, Q, clk, clr
endmodule
