// Logisim project 2-bit_Arithmetic.circ as structural Verilog: 1 circuit, main circuit 2-bitArithmetic
module _2_bitArithmetic (
  input  Cin,
  input  S0,
  input  S1,
  input  [1:0] A_i,
  input  [1:0] B_i,
  output D_i,
  output D_i_1,
  output C_i_2
);

  wire n1_bit_arithmetic_1_c_i_1;

  _1_bit_Arithmetic u_1_bit_arithmetic_1 (
    .Cin(Cin), .S0(S0), .S1(S1), .A_i(A_i[0]), .B_i(B_i[0]), .D_i(D_i), .C_i_1(n1_bit_arithmetic_1_c_i_1));
  _1_bit_Arithmetic u_1_bit_arithmetic_2 (
    .Cin(n1_bit_arithmetic_1_c_i_1), .S0(S0), .S1(S1), .A_i(A_i[1]), .B_i(B_i[1]), .D_i(D_i_1), .C_i_1(C_i_2));
endmodule
