// Logisim project 2-bit_logic.circ as structural Verilog: 2 circuits, main circuit 1-bit_Logic
module _1_bit_Logic (
  input  [1:0] S1_S0,
  input  A_i,
  input  B_i,
  output F_i
);

  wire and_1_out, not_1_out, or_1_out, xor_1_out;

  and and_1 (and_1_out, A_i, B_i);
  or or_1 (or_1_out, A_i, B_i);
  xor xor_1 (xor_1_out, A_i, B_i);
  not not_1 (not_1_out, A_i);
  Multiplexer #(.select(2)) multiplexer_1 (
    .in0(and_1_out), .in1(or_1_out), .in2(xor_1_out), .in3(not_1_out), .out(F_i), .sel(S1_S0));  // open: en
endmodule

module _2_bit_Logic (
  input  [1:0] S1_S0,
  input  [1:0] A,
  input  [1:0] B,
  output F_i,
  output F_i_1
);

  _1_bit_logic_1_bit_Logic u_1_bit_logic_1 (.S1_S0(S1_S0), .A_i(A[0]), .B_i(B[0]), .F_i(F_i));
  _1_bit_logic_1_bit_Logic u_1_bit_logic_2 (.S1_S0(S1_S0), .A_i(A[1]), .B_i(B[1]), .F_i(F_i_1));
endmodule
