// Logisim project 4-bit_Arithmetic.circ as structural Verilog: 1 circuit, main circuit main
module main (
  input  C_in,
  input  S0,
  input  S1,
  input  [3:0] A,
  input  [3:0] B,
  output C_out,
  output [3:0] Z
);

  wire n1_bit_arithmetic_1_c_i_1, n1_bit_arithmetic_2_c_i_1, n1_bit_arithmetic_3_c_i_1;

  _1_bit_Arithmetic u_1_bit_arithmetic_1 (
    .Cin(C_in), .S0(S0), .S1(S1), .A_i(A[0]), .B_i(B[0]), .D_i(Z[0]), .C_i_1(n1_bit_arithmetic_1_c_i_1));
  _1_bit_Arithmetic u_1_bit_arithmetic_2 (
    .Cin(n1_bit_arithmetic_1_c_i_1), .S0(S0), .S1(S1), .A_i(A[1]), .B_i(B[1]), .D_i(Z[1]),
    .C_i_1(n1_bit_arithmetic_2_c_i_1));
  _1_bit_Arithmetic u_1_bit_arithmetic_3 (
    .Cin(n1_bit_arithmetic_2_c_i_1), .S0(S0), .S1(S1), .A_i(A[2]), .B_i(B[2]), .D_i(Z[2]),
    .C_i_1(n1_bit_arithmetic_3_c_i_1));
  _1_bit_Arithmetic u_1_bit_arithmetic_4 (
    .Cin(n1_bit_arithmetic_3_c_i_1), .S0(S0), .S1(S1), .A_i(A[3]), .B_i(B[3]), .D_i(Z[3]), .C_i_1(C_out));
endmodule
