// Logisim project 4-bit_register.circ as structural Verilog: 1 circuit, main circuit main
module main (
  input  [7:0] Bus_Input,
  input  [1:0] S1_S0,
  input  increment,
  input  Load,
  input  CLR,
  output C_out,
  output [3:0] Z
);

  wire or_1_out;
  wire [3:0] main_1_z, multiplexer_1_out;

  _4_bit_Arithmetic_main main_1 (
    .C_in(1'b0), .S0(S1_S0[0]), .S1(S1_S0[1]), .A(Z), .B(4'b1111), .C_out(C_out), .Z(main_1_z));
  Multiplexer #(.width(4)) multiplexer_1 (
    .in0(Bus_Input[3:0]), .in1(main_1_z), .out(multiplexer_1_out), .sel(increment));  // open: en
  or or_1 (or_1_out, increment, Load);
  Register #(.width(4)) register_1 (.D(multiplexer_1_out), .Q(Z), .clk(or_1_out), .clr(CLR));  // open: en
endmodule
