// Logisim project 8-bit-Shifter.circ as structural Verilog: 1 circuit, main circuit main
module main (
  input  A_i_1,
  input  [7:0] A,
  input  A_i_1_2,
  output [7:0] SHL,
  output [7:0] SHR
);


  assign SHL = {A[6:0], A_i_1};
  assign SHR = {A_i_1_2, A[7:1]};
endmodule
