// Logisim project 8-bit_ALSU.circ as structural Verilog: 1 circuit, main circuit main
module main (
  input  C_in,
  input  A_i_1,
  input  A_i_1_2,
  input  [1:0] MUX_select,
  input  [7:0] A,
  input  [7:0] B,
  input  [1:0] S1_S0,
  output E,
  output [7:0] X
);

  wire [7:0] Arithmetic_z, Logical_z, Shift_shl, Shift_shr;

  _8_bit_Arithmetic_main Arithmetic (
    .C_in(C_in), .S0(S1_S0[0]), .S1(S1_S0[1]), .A(A), .B(B), .Z(Arithmetic_z), .C_out(E));
  _8_bit_logic_main Logical (.in_1(S1_S0), .A(A), .B(B), .Z(Logical_z));
  _8_bit_Shifter_main Shift (.A_i_1(A_i_1), .A(A), .A_i_1_2(A_i_1_2), .SHL(Shift_shl), .SHR(Shift_shr));
  Multiplexer #(.select(2), .width(8)) multiplexer_1 (
    .in0(Arithmetic_z), .in1(Logical_z), .in2(Shift_shl), .in3(Shift_shr), .out(X), .sel(MUX_select));  // open: en

  // Other names for the same wires on the sheet: S[1:0] = S1_S0; S0 = S1_S0[0]; S1 = S1_S0[1]
endmodule
