// Logisim project 8-bit_Arithmetic.circ as structural Verilog: 1 circuit, main circuit main
module main (
  input  C_in,
  input  S0,
  input  S1,
  input  [7:0] A,
  input  [7:0] B,
  output [7:0] Z,
  output C_out
);

  wire n1_bit_arithmetic_1_c_i_1, n1_bit_arithmetic_2_c_i_1, n1_bit_arithmetic_3_c_i_1,
       n1_bit_arithmetic_4_c_i_1, n1_bit_arithmetic_5_c_i_1, n1_bit_arithmetic_6_c_i_1,
       n1_bit_arithmetic_7_c_i_1;

  _1_bit_Arithmetic u_1_bit_arithmetic_1 (
    .Cin(C_in), .S0(S0), .S1(S1), .A_i(A[0]), .B_i(B[0]), .D_i(Z[0]), .C_i_1(n1_bit_arithmetic_1_c_i_1));
  _1_bit_Arithmetic u_1_bit_arithmetic_2 (
    .Cin(n1_bit_arithmetic_1_c_i_1), .S0(S0), .S1(S1), .A_i(A[1]), .B_i(B[1]), .D_i(Z[1]),
    .C_i_1(n1_bit_arithmetic_2_c_i_1));
  _1_bit_Arithmetic u_1_bit_arithmetic_3 (
    .Cin(n1_bit_arithmetic_2_c_i_1), .S0(S0), .S1(S1), .A_i(A[2]), .B_i(B[2]), .D_i(Z[2]),
    .C_i_1(n1_bit_arithmetic_3_c_i_1));
  _1_bit_Arithmetic u_1_bit_arithmetic_4 (
    .Cin(n1_bit_arithmetic_3_c_i_1), .S0(S0), .S1(S1), .A_i(A[3]), .B_i(B[3]), .D_i(Z[3]),
    .C_i_1(n1_bit_arithmetic_4_c_i_1));
  _1_bit_Arithmetic u_1_bit_arithmetic_5 (
    .Cin(n1_bit_arithmetic_4_c_i_1), .S0(S0), .S1(S1), .A_i(A[4]), .B_i(B[4]), .D_i(Z[4]),
    .C_i_1(n1_bit_arithmetic_5_c_i_1));
  _1_bit_Arithmetic u_1_bit_arithmetic_6 (
    .Cin(n1_bit_arithmetic_5_c_i_1), .S0(S0), .S1(S1), .A_i(A[5]), .B_i(B[5]), .D_i(Z[5]),
    .C_i_1(n1_bit_arithmetic_6_c_i_1));
  _1_bit_Arithmetic u_1_bit_arithmetic_7 (
    .Cin(n1_bit_arithmetic_6_c_i_1), .S0(S0), .S1(S1), .A_i(A[6]), .B_i(B[6]), .D_i(Z[6]),
    .C_i_1(n1_bit_arithmetic_7_c_i_1));
  _1_bit_Arithmetic u_1_bit_arithmetic_8 (
    .Cin(n1_bit_arithmetic_7_c_i_1), .S0(S0), .S1(S1), .A_i(A[7]), .B_i(B[7]), .D_i(Z[7]), .C_i_1(C_out));
endmodule
