// Logisim project 8-bit_logic.circ as structural Verilog: 1 circuit, main circuit main
module main (
  input  [1:0] in_1,
  input  [7:0] A,
  input  [7:0] B,
  output [7:0] Z
);

  _1_bit_Logic u_1_bit_logic_1 (.S1_S0(in_1), .A_i(A[0]), .B_i(B[0]), .F_i(Z[0]));
  _1_bit_Logic u_1_bit_logic_2 (.S1_S0(in_1), .A_i(A[1]), .B_i(B[1]), .F_i(Z[1]));
  _1_bit_Logic u_1_bit_logic_3 (.S1_S0(in_1), .A_i(A[2]), .B_i(B[2]), .F_i(Z[2]));
  _1_bit_Logic u_1_bit_logic_4 (.S1_S0(in_1), .A_i(A[3]), .B_i(B[3]), .F_i(Z[3]));
  _1_bit_Logic u_1_bit_logic_5 (.S1_S0(in_1), .A_i(A[4]), .B_i(B[4]), .F_i(Z[4]));
  _1_bit_Logic u_1_bit_logic_6 (.S1_S0(in_1), .A_i(A[5]), .B_i(B[5]), .F_i(Z[5]));
  _1_bit_Logic u_1_bit_logic_7 (.S1_S0(in_1), .A_i(A[6]), .B_i(B[6]), .F_i(Z[6]));
  _1_bit_Logic u_1_bit_logic_8 (.S1_S0(in_1), .A_i(A[7]), .B_i(B[7]), .F_i(Z[7]));

  // Other names for the same wires on the sheet: S[1:0] = in_1
endmodule
