// Logisim project 8-bit_register.circ as structural Verilog: 1 circuit, main circuit main
module main (
  input  [7:0] Bus_Input,
  input  [1:0] S1_S0,
  input  increment,
  input  Load,
  input  CLR,
  output [7:0] Z,
  output C_out
);

  wire or_1_out;
  wire [7:0] main_1_z, multiplexer_1_out;

  _8_bit_Arithmetic_main main_1 (
    .C_in(1'b0), .S0(S1_S0[0]), .S1(S1_S0[1]), .A(Z), .B({8{1'b1}}), .Z(main_1_z), .C_out(C_out));
  Multiplexer #(.width(8)) multiplexer_1 (
    .in0(Bus_Input), .in1(main_1_z), .out(multiplexer_1_out), .sel(increment));  // open: en
  or or_1 (or_1_out, increment, Load);
  Register register_1 (.D(multiplexer_1_out), .Q(Z), .clk(or_1_out), .clr(CLR));  // open: en
endmodule
