// Logisim project AC_control.circ as structural Verilog: 1 circuit, main circuit main
module main (
  input  T5,
  input  D0,
  input  D1,
  input  D2,
  input  D7,
  input  T3,
  input  I,
  input  B7,
  input  B6,
  input  B9,
  input  B11,
  input  B5,
  output AC_LD,
  output AC_CLR,
  output AC_INC
);

  wire and_1_out, and_2_out, and_3_out, and_4_out, and_5_out, and_6_out, and_7_out, not_1_out;

  not not_1 (not_1_out, I);
  and and_1 (and_1_out, T5, D0);
  and and_2 (and_2_out, T5, D1);
  and and_3 (and_3_out, T5, D2);
  and and_4 (and_4_out, D7, T3, not_1_out);
  and and_5 (and_5_out, and_4_out, B7);
  and and_6 (and_6_out, and_4_out, B6);
  and and_7 (and_7_out, and_4_out, B9);
  and and_8 (AC_CLR, and_4_out, B11);
  and and_9 (AC_INC, and_4_out, B5);
  or or_1 (AC_LD, and_1_out, and_2_out, and_3_out, and_5_out, and_6_out, and_7_out);
endmodule
