// Logisim project B.circ as structural Verilog: 1 circuit, main circuit main
module main (
  input  [3:0] IR_3_0,
  output B0,
  output B1,
  output B2,
  output B3,
  output B4,
  output B5,
  output B6,
  output B7,
  output B11,
  output B10,
  output B9,
  output B8
);

  wire decoder_1_out12, decoder_1_out13, decoder_1_out14, decoder_1_out15;

  Decoder #(.select(4)) decoder_1 (
    .out0(B0), .out1(B1), .out2(B2), .out3(B3), .out4(B4), .out5(B5), .out6(B6), .out7(B7), .out8(B8),
    .out9(B9), .out10(B10), .out11(B11), .out12(decoder_1_out12), .out13(decoder_1_out13),
    .out14(decoder_1_out14), .out15(decoder_1_out15), .sel(IR_3_0));  // open: en
endmodule
