// Logisim project Bus.circ as structural Verilog: 1 circuit, main circuit main
module main (
  input  [2:0] Select,
  input  PC_INC,
  input  PC_LD,
  input  PC_CLR,
  input  OUTR_LD,
  input  S0,
  input  TR_INC,
  input  TR_LD,
  input  IR_INC,
  input  TR_CLR,
  input  IR_LD,
  input  C_in,
  input  IR_CLR,
  input  A_i_1,
  input  DR_INC,
  input  A_i_1_2,
  input  DR_LD,
  input  [1:0] A_SELECT,
  input  DR_CLR,
  input  [1:0] ALSU_SELECT,
  input  AC_INC,
  input  AC_LD,
  input  AC_CLR,
  input  RAM_CLR,
  input  AR_INC,
  input  RAM_LD,
  input  AR_LD,
  input  AR_CLR,
  output [7:0] IR_output,
  output [7:0] DR_output,
  output E,
  output AC_0,
  output AC_7,
  output FGI
);

  wire CLK, main_1_e;
  wire [3:0] AR_4, PC;
  wire [6:1] AC;
  wire [7:0] AR, B, Bus, INPR, main_1_x, OUTR, TR;

  Clock clock_1 (.out(CLK));
  _8_bit_register_main DR (.increment(1'b0), .Load(OUTR_LD), .CLK(CLK), .Bus_Input(Bus), .CLR(1'b0), .Z(OUTR));
  _8_bit_register_main IR (.increment(IR_INC), .Load(IR_LD), .CLK(CLK), .Bus_Input(Bus), .CLR(IR_CLR), .Z(IR_output));
  RAM #(.addrWidth(4)) ram_1 (.addr(AR_4), .data(Bus), .sel(1'b1), .clk(CLK), .ld(RAM_LD), .clr(RAM_CLR));
  _4_bit_register_main u_PC (.increment(PC_INC), .Load(PC_LD), .CLK(CLK), .Bus_Input(Bus), .CLR(PC_CLR), .Z(PC));
  _8_bit_register_main u_TR (.increment(TR_INC), .Load(TR_LD), .CLK(CLK), .Bus_Input(Bus), .CLR(TR_CLR), .Z(TR));
  _8_bit_register_main DR_2 (.increment(DR_INC), .Load(DR_LD), .CLK(CLK), .Bus_Input(Bus), .CLR(DR_CLR), .Z(DR_output));
  Keyboard keyboard_1 (.clk(CLK), .re(1'b1), .clr(1'b0), .avail(FGI), .data(Bus[6:0]));
  _8_bit_register_main INPUT (.increment(1'b0), .Load(1'b0), .CLK(CLK), .Bus_Input(Bus), .CLR(1'b0), .Z(INPR));
  Multiplexer #(.select(3), .width(8)) multiplexer_1 (
    .in1(AR), .in2({4'b0000, PC}), .in3(DR_output), .in4({AC_7, AC, AC_0}), .in5(IR_output), .in6(TR),
    .in7(Bus), .out(Bus), .sel(Select));  // open: in0, en
  _8_bit_ALSU_main main_1 (
    .A_i_1(A_i_1), .A_i_1_2(A_i_1_2), .MUX_select(A_SELECT), .A({AC_7, AC, AC_0}), .B(B),
    .S1_S0(ALSU_SELECT), .C_in(C_in), .E(main_1_e), .X(main_1_x));
  _4_bit_register_main u_AR (.increment(AR_INC), .Load(AR_LD), .CLK(CLK), .Bus_Input(Bus), .CLR(AR_CLR), .Z(AR_4));
  Hex_Digit_Display hex_digit_display_1 (.value(OUTR[7:4]));  // open: dp
  Multiplexer #(.width(8)) multiplexer_2 (.in0(INPR), .in1(DR_output), .out(B), .en(S0));  // open: sel
  Hex_Digit_Display hex_digit_display_2 (.value(OUTR[3:0]));  // open: dp
  D_Flip_Flop d_ff_1 (.clk(CLK), .D(main_1_e), .Q(E));  // open: Qn, preset, en, reset
  _8_bit_register_main u_AC (
    .increment(AC_INC), .Load(AC_LD), .CLK(CLK), .Bus_Input(main_1_x), .CLR(AC_CLR), .Z({AC_7, AC, AC_0}));
  // also tied to GND on the sheet: Bus[7]

  // Other names for the same wires on the sheet: AC (some bits) = {AC_7, AC_0}; AR_8[3:0] = AR_4; DR[7:0] = DR_output;
  //   IR[7:0] = IR_output; INPUT[7:0] = Bus; RAM[7:0] = Bus
endmodule
