// Logisim project CPU.circ as structural Verilog: 1 circuit, main circuit main
module main (
  input  Master_CLR,
  input  C_in,
  input  S,
  input  A_i_1,
  input  S0,
  input  A_i_1_2,
  input  [1:0] A_SELECT,
  input  [1:0] ALSU_SELECT
);

  wire AC_0, AC_7, AC_CLR, AC_INC, AC_LD, AR_CLR, AR_INC, AR_LD, CLK, d_ff_1_q, DR_INC, DR_LD, DR_ZERO, E,
       FGI, FGO, IEN, IR_INC, IR_LD, MASTER_CLK_out, ON_OFF_out, OUTR_LD, PC_CLR, PC_INC, PC_LD, RD, SC_CLR,
       TR_INC, TR_LD, WR;
  wire [2:0] SEL;
  wire [7:0] BUS_dr_output, IR;

  Clock MASTER_CLK (.out(MASTER_CLK_out));
  Button ON_OFF (.out(ON_OFF_out));
  D_Flip_Flop d_ff_1 (.clk(MASTER_CLK_out), .D(S), .Q(d_ff_1_q), .preset(ON_OFF_out));  // open: Qn, en, reset
  // CU_main CU: pin names not known; wires that end beside it: E, CLK, FGI, FGO, DR_ZERO, IR, AC_7, AC_0, AC_LD, RD, SC_CLR, AC_CLR, WR, AC_INC, TR_LD, AR_LD, AR_CLR, AR_INC, PC_LD, PC_CLR, PC_INC, OUTR_LD, FGO, IEN, DR_LD, DR_INC, IR_LD
  and and_1 (CLK, MASTER_CLK_out, d_ff_1_q);
  Bus_main BUS (
    .Select(SEL), .PC_INC(PC_INC), .PC_LD(PC_LD), .OUTR_LD(OUTR_LD), .S0(S0), .TR_INC(TR_INC), .TR_LD(TR_LD),
    .IR_INC(IR_INC), .IR_LD(IR_LD), .A_i_1(A_i_1), .DR_INC(DR_INC), .A_i_1_2(A_i_1_2), .DR_LD(DR_LD),
    .A_SELECT(A_SELECT), .ALSU_SELECT(ALSU_SELECT), .AC_INC(AC_INC), .AC_LD(AC_LD), .AR_INC(AR_INC),
    .AR_LD(AR_LD), .AR_CLR(AR_CLR), .IR_output(IR), .C_in(C_in), .IR_CLR(Master_CLR), .RAM_LD(WR),
    .RAM_CLR(Master_CLR), .DR_CLR(Master_CLR), .TR_CLR(Master_CLR), .out_34(FGI), .AC_CLR(AC_CLR),
    .PC_CLR(PC_CLR), .DR_output(BUS_dr_output), .E(E), .AC_0(AC_0), .AC_7(AC_7));
  Zero_Detector_main ZERO (.in_1(BUS_dr_output), .Zero(DR_ZERO));

  // Other names for the same wires on the sheet: M_CLR = Master_CLR
endmodule
