// Logisim project CU.circ as structural Verilog: 1 circuit, main circuit main
module main (
  input  E,
  input  clk_in,
  input  FGI,
  input  FGO,
  input  DR_ZERO,
  input  AC_7,
  input  AC_ZERO,
  input  [7:0] IR,
  output AC_LD,
  output RD,
  output SC_CLR,
  output AC_CLR,
  output WR,
  output AC_INC,
  output TR_LD,
  output AR_LD,
  output AR_CLR,
  output AR_INC,
  output PC_LD,
  output PC_CLR,
  output PC_INC,
  output OUTR_LD,
  output FGO_2,
  output IEN,
  output DR_LD,
  output DR_INC,
  output IR_LD
);

  wire B0, B1, B2, B3, B4, B5, B6, B7, B8, B9, B10, B11, D0, D1, D2, D3, D4, D5, D6, D7, R, T0, T1, T2, T3,
       T4, T5, T6;

  SC_Opcode_Decoder_main main_1 (
    .clk_in(clk_in), .Op_code(IR[6:4]), .T0(T0), .T1(T1), .T2(T2), .T3(T3), .T4(T4), .T5(T5), .T6(T6),
    .D0(D0), .D1(D1), .D2(D2), .D3(D3), .D4(D4), .D5(D5), .D6(D6), .D7(D7));
  B_main B (
    .B0(B0), .B1(B1), .B2(B2), .B3(B3), .B4(B4), .B5(B5), .B6(B6), .B7(B7), .IR_3_0(IR[3:0]), .B11(B11),
    .B10(B10), .B9(B9), .B8(B8));
  IEN_control_main u_IEN (.D7(D7), .I(IR[7]), .T3(T3), .B7(B7), .B6(B6), .R(R), .T2(T2), .CLK(clk_in), .IEN(IEN));
  IR_control_main main_2 (.R(R), .T1(T1), .IR_LD(IR_LD));
  R_control_main u_R (.T0(T0), .T1(T1), .T2(T2), .IEN(IEN), .FGI(FGI), .FGO(FGO), .R(R));
  AC_control_main AC (
    .T5(T5), .D0(D0), .D1(D1), .D2(D2), .D7(D7), .T3(T3), .I(IR[7]), .B7(B7), .B6(D2), .B9(D1), .B11(D0),
    .B5(T5), .AC_LD(AC_LD), .AC_CLR(AC_CLR), .AC_INC(AC_INC));
  AR_control_main AR (
    .D7(D7), .I(IR[7]), .T3(T3), .T2(T2), .T0(T0), .R(R), .D5(D5), .T4(T4), .AR_LD(AR_LD), .AR_CLR(AR_CLR),
    .AR_INR(AR_INC));
  // MEM_control_main MEM: pin names not known; wires that end beside it: R, T1, T4, D0, D1, D2, D6, IR[7], T3, D7, D3, D5, D6, T6, RD, WR
  PC_control_main PC (
    .R(R), .T1(T1), .T4(T4), .D4(D4), .T5(T5), .D5(D5), .T2(T2), .T6(T6), .D6(D6), .DR_ZERO(DR_ZERO),
    .D7(D7), .T3(T3), .I(IR[7]), .B9(B9), .FGI(FGI), .B8(B8), .FGO(FGO), .B4(B4), .AC_7(AC_7), .B3(B3),
    .B2(B2), .AC_ZERO(AC_ZERO), .B1(B1), .E(E), .PC_CLR(PC_LD), .PC_LD(PC_CLR), .PC_INC(PC_INC));
  DR_control_main main_3 (.T4(T4), .D0(D0), .D1(D1), .D2(D2), .D6(D6), .T5(T5), .DR_LD(DR_LD), .DR_INC(DR_INC));
  SC_control_main SC (
    .R(R), .T2(T2), .D0(D0), .T5(T5), .D1(D1), .D2(D2), .D5(D5), .D3(D3), .T4(T4), .D4(D4), .D7(D7),
    .I(IR[7]), .T3(T3), .SC_CLR(SC_CLR));
  TR_control_main TR (.R(R), .T0(T0), .TR_LD(TR_LD));
  OUTR_control_main OUTR (.D7(D7), .I(IR[7]), .T3(T3), .B10(B10), .OUTR_LD(OUTR_LD), .FGO(FGO_2));

  // Other names for the same wires on the sheet: CLK = clk_in; IR_0_3[3:0] = IR[3:0]; Opcode[2:0] = IR[6:4];
  //   I = IR[7]
endmodule
