// Logisim project IEN_control.circ as structural Verilog: 1 circuit, main circuit main
module main (
  input  D7,
  input  I,
  input  T3,
  input  B7,
  input  B6,
  input  R,
  input  T2,
  input  CLK,
  output IEN
);

  wire and_1_out, and_2_out, and_3_out, and_4_out, or_1_out;

  and and_1 (and_1_out, D7, I, T3);
  and and_2 (and_2_out, and_1_out, B7);
  and and_3 (and_3_out, and_1_out, B6);
  and and_4 (and_4_out, R, T2);
  or or_1 (or_1_out, and_2_out, and_3_out);
  J_K_Flip_Flop j_k_ff_1 (.J(or_1_out), .clk(CLK), .K(and_4_out), .Q(IEN));  // open: Qn, preset, en, reset
endmodule
