// Logisim project IR_control.circ as structural Verilog: 1 circuit, main circuit main
module main (
  input  R,
  input  T1,
  output IR_LD
);

  wire not_1_out;

  not not_1 (not_1_out, R);
  and and_1 (IR_LD, not_1_out, T1);
endmodule
