// Logisim project MEM_control.circ as structural Verilog: 1 circuit, main circuit main
module main (
  input  R,
  input  T1,
  input  T4,
  input  D0,
  input  D1,
  input  D2,
  input  D2_2,
  input  I,
  input  T3,
  input  D7,
  input  D3,
  input  D5,
  input  D6,
  input  T6,
  output RD,
  output WR
);

  wire and_1_out, and_2_out, and_3_out, and_4_out, and_5_out, and_6_out, and_7_out, and_8_out, and_9_out,
       and_10_out, not_1_out, not_2_out;

  not not_1 (not_1_out, D7);
  not not_2 (not_2_out, R);
  and and_1 (and_1_out, not_2_out, T1);
  and and_2 (and_2_out, T4, D0);
  and and_3 (and_3_out, T4, D1);
  and and_4 (and_4_out, T4, D2);
  and and_5 (and_5_out, T4, D2_2);
  and and_6 (and_6_out, I, T3, not_1_out);
  and and_7 (and_7_out, R, T1);
  and and_8 (and_8_out, D3, T4);
  and and_9 (and_9_out, D5, T4);
  and and_10 (and_10_out, D6, T6);
  or or_1 (RD, and_1_out, and_2_out, and_3_out, and_4_out, and_5_out, and_6_out);
  or or_2 (WR, and_7_out, and_8_out, and_9_out, and_10_out);
endmodule
