// Logisim project OUTR_control.circ as structural Verilog: 1 circuit, main circuit main
module main (
  input  D7,
  input  I,
  input  T3,
  input  B10,
  output OUTR_LD,
  output FGO
);

  wire and_1_out;

  and and_1 (and_1_out, D7, I, T3);
  and and_2 (FGO, and_1_out, B10);

  assign OUTR_LD = FGO;
endmodule
