// Logisim project PC_control.circ as structural Verilog: 1 circuit, main circuit main
// PC_INC
module main (
  input  R,
  input  T1,
  input  T4,
  input  D4,
  input  T5,
  input  D5,
  input  T2,
  input  T6,
  input  D6,
  input  DR_ZERO,
  input  D7,
  input  T3,
  input  I,
  input  B9,
  input  FGI,
  input  B8,
  input  FGO,
  input  B4,
  input  AC_15,
  input  B3,
  input  B2,
  input  AC_ZERO,
  input  B1,
  input  E,
  output PC_CLR,
  output PC_LD,
  output PC_INC
);

  wire and_2_out, and_3_out, and_4_out, and_5_out, and_6_out, and_7_out, and_8_out, and_9_out, and_10_out,
       and_11_out, and_12_out, and_13_out, and_14_out, not_1_out, not_2_out, not_3_out, not_4_out;

  not not_1 (not_1_out, R);
  not not_2 (not_2_out, I);
  and and_1 (PC_CLR, R, T1);
  and and_2 (and_2_out, not_1_out, T1);
  and and_3 (and_3_out, T4, D4);
  and and_4 (and_4_out, T5, D5);
  and and_5 (and_5_out, R, T2);
  and and_6 (and_6_out, T6, D6, DR_ZERO);
  and and_7 (and_7_out, D7, T3, I);
  and and_8 (and_8_out, not_2_out, D7, T3);
  or or_1 (PC_LD, and_3_out, and_4_out);
  and and_9 (and_9_out, and_7_out, B9, FGI);
  and and_10 (and_10_out, and_7_out, B8, FGO);
  not not_3 (not_3_out, E);
  not not_4 (not_4_out, AC_15);
  and and_11 (and_11_out, B4, not_4_out, and_8_out);
  and and_12 (and_12_out, and_8_out, AC_15, B3);
  and and_13 (and_13_out, B2, and_8_out, AC_ZERO);
  and and_14 (and_14_out, and_8_out, B1, not_3_out);
  or or_2 (PC_INC, and_2_out, and_5_out, and_6_out, and_9_out, and_10_out, and_11_out, and_12_out, and_13_out, and_14_out);

  // Notes on the sheet:
  //   p
  //   r
endmodule
