// Logisim project R_control.circ as structural Verilog: 1 circuit, main circuit main
module main (
  input  T0,
  input  T1,
  input  T2,
  input  IEN,
  input  FGI,
  input  FGO
);

  wire and_1_out, and_2_out, j_k_ff_1_q, not_1_out, not_2_out, not_3_out, or_1_out;

  not not_1 (not_1_out, T0);
  not not_2 (not_2_out, T1);
  not not_3 (not_3_out, T2);
  or or_1 (or_1_out, FGI, FGO);
  and and_1 (and_1_out, T2, j_k_ff_1_q);
  and and_2 (and_2_out, not_1_out, not_2_out, not_3_out, IEN, or_1_out);
  J_K_Flip_Flop j_k_ff_1 (.J(and_2_out), .K(and_1_out), .Q(j_k_ff_1_q));  // open: clk, Qn, preset, en, reset
endmodule
