// Logisim project SC+Opcode_Decoder.circ as structural Verilog: 1 circuit, main circuit main
module main (
  input  clk_in,
  input  [2:0] Op_code,
  output T0,
  output T1,
  output T2,
  output T3,
  output T4,
  output T5,
  output T6,
  output D0,
  output D1,
  output D2,
  output D3,
  output D4,
  output D5,
  output D6,
  output D7
);

  wire [2:0] counter_1_q;

  Decoder #(.select(3)) decoder_1 (
    .out0(D0), .out1(D1), .out2(D2), .out3(D3), .out4(D4), .out5(D5), .out6(D6), .out7(D7), .sel(Op_code));  // open: en
  Counter #(.width(3), .max('h5)) counter_1 (.Q(counter_1_q), .clk(clk_in));  // open: load, D, count, carry, clr
  Decoder #(.select(3)) decoder_2 (
    .out0(T0), .out1(T1), .out2(T2), .out3(T3), .out4(T4), .out5(T5), .out6(T6), .sel(counter_1_q));  // open: out7, en
endmodule
