// Logisim project SC_control.circ as structural Verilog: 1 circuit, main circuit main
module main (
  input  R,
  input  T2,
  input  D0,
  input  T5,
  input  D1,
  input  D2,
  input  D5,
  input  D3,
  input  T4,
  input  D4,
  input  D7,
  input  I,
  input  T3,
  output SC_CLR
);

  wire and_1_out, and_2_out, and_3_out, and_4_out, and_5_out, and_6_out, and_7_out, and_8_out, and_9_out,
       not_1_out;

  and and_1 (and_1_out, R, T2);
  and and_2 (and_2_out, D0, T5);
  and and_3 (and_3_out, D1, T5);
  and and_4 (and_4_out, D2, T5);
  and and_5 (and_5_out, D5, T5);
  and and_6 (and_6_out, D3, T4);
  and and_7 (and_7_out, D4, T4);
  not not_1 (not_1_out, I);
  and and_8 (and_8_out, D7, I, T3);
  and and_9 (and_9_out, D7, not_1_out, T3);
  or or_1 (SC_CLR, and_1_out, and_2_out, and_3_out, and_4_out, and_5_out, and_6_out, and_7_out, and_8_out, and_9_out);
endmodule
